// Logisim project J.circ as structural Verilog
module tonghuo_men (
  input  in_1,
  input  in_2,
  output out_3
);

  wire nand_1_out, or_1_out;

  or or_1 (or_1_out, in_1, in_2);
  nand nand_1 (nand_1_out, in_1, in_2);
  nand nand_2 (out_3, or_1_out, nand_1_out);
endmodule

module yihuo_men (
  input  in_1,
  input  in_2,
  output out_3
);

  wire and_1_out, nor_1_out;

  and and_1 (and_1_out, in_1, in_2);
  nor nor_1 (nor_1_out, in_1, in_2);
  nor nor_2 (out_3, and_1_out, nor_1_out);
endmodule

module huomen (
  input  in_1,
  input  in_2,
  output out_3
);

  wire transistor_1_out, transistor_2_out;

  Transistor transistor_1 (.in(1'b1), .out(transistor_1_out), .gate(in_1));
  Transistor transistor_2 (.in(transistor_1_out), .out(transistor_2_out), .gate(in_2));
  Transistor #(.\type ("n")) transistor_3 (.in(1'b0), .out(transistor_2_out), .gate(in_1));
  Transistor #(.\type ("n")) transistor_4 (.in(1'b0), .out(transistor_2_out), .gate(in_2));
  Transistor transistor_5 (.in(1'b1), .out(out_3), .gate(transistor_2_out));
  Transistor #(.\type ("n")) transistor_6 (.in(1'b0), .out(out_3), .gate(transistor_2_out));
endmodule

module tonghuo_quan (
  input  in_1,
  input  in_2,
  output out_3
);

  wire transistor_1_out;

  Transistor transistor_1 (.in(1'b1), .out(transistor_1_out), .gate(in_2));
  Transistor #(.\type ("n")) transistor_2 (.in(1'b0), .out(transistor_1_out), .gate(in_2));
  Transistor transistor_3 (.in(transistor_1_out), .out(out_3), .gate(in_1));
  Transistor #(.\type ("n")) transistor_4 (.in(in_2), .out(out_3), .gate(in_1));
  // Transmission_Gate transmission_1: pin names not known; wires that end beside it: out_3, transistor_1_out, in_2, in_1
endmodule

module yihuo_quan (
  input  in_1,
  input  in_2,
  output out_3
);

  wire transistor_3_out;

  Transistor transistor_1 (.in(in_2), .out(out_3), .gate(in_1));
  Transistor #(.\type ("n")) transistor_2 (.in(transistor_3_out), .out(out_3), .gate(in_1));
  Transistor transistor_3 (.in(1'b1), .out(transistor_3_out), .gate(in_2));
  Transistor #(.\type ("n")) transistor_4 (.in(1'b0), .out(transistor_3_out), .gate(in_2));
  // Transmission_Gate transmission_1: pin names not known; wires that end beside it: out_3, in_2, transistor_3_out, in_1
endmodule

module yimaqi2to4 (
  input  in_1,
  input  in_2,
  input  in_3,
  output out_4,
  output out_5,
  output out_6,
  output out_7
);

  and and_1 (out_4, ~in_1, in_3, ~in_2);  // AND_Gate
  and and_2 (out_5, in_1, in_3, ~in_2);  // AND_Gate
  and and_3 (out_6, ~in_1, in_3, in_2);  // AND_Gate
  and and_4 (out_7, in_1, in_3, in_2);
endmodule

module yimaqi3to8 (
  input  zero,
  input  one,
  input  two,
  input  en,
  output out_5,
  output out_6,
  output out_7,
  output out_8,
  output out_9,
  output out_10,
  output out_11,
  output out_12
);

  wire and_1_out, and_2_out, not_1_out, yimaqi2to4_1_out_4, yimaqi2to4_2_out_4;

  and and_1 (and_1_out, en, zero);
  and and_2 (and_2_out, one, en);
  not not_1 (not_1_out, two);
  yimaqi2to4 yimaqi2to4_1 (
    .in_1(and_1_out), .in_2(and_2_out), .in_3(not_1_out), .out_4(yimaqi2to4_1_out_4), .out_5(out_6),
    .out_6(out_7), .out_7(out_8));
  yimaqi2to4 yimaqi2to4_2 (
    .in_1(and_1_out), .in_2(and_2_out), .in_3(two), .out_4(yimaqi2to4_2_out_4), .out_5(out_10),
    .out_6(out_11), .out_7(out_12));
  and and_3 (out_9, en, yimaqi2to4_2_out_4);
  and and_4 (out_5, en, yimaqi2to4_1_out_4);
endmodule

module shumaguanyimaqi10 (
  input  in_1,
  input  in_2,
  input  in_3,
  input  in_4
);

  wire and_1_out, and_2_out, or_1_out, or_2_out, or_3_out, or_4_out, or_5_out, or_6_out, or_7_out,
       yimaqi3to8_1_out_5, yimaqi3to8_1_out_6, yimaqi3to8_1_out_7, yimaqi3to8_1_out_8, yimaqi3to8_1_out_9,
       yimaqi3to8_1_out_10, yimaqi3to8_1_out_11, yimaqi3to8_1_out_12;

  yimaqi3to8 yimaqi3to8_1 (
    .zero(in_1), .one(in_2), .two(in_3), .en(1'b1), .out_5(yimaqi3to8_1_out_5), .out_6(yimaqi3to8_1_out_6),
    .out_7(yimaqi3to8_1_out_7), .out_8(yimaqi3to8_1_out_8), .out_9(yimaqi3to8_1_out_9),
    .out_10(yimaqi3to8_1_out_10), .out_11(yimaqi3to8_1_out_11), .out_12(yimaqi3to8_1_out_12));
  and and_1 (and_1_out, ~in_1, in_4);  // AND_Gate
  and and_2 (and_2_out, in_1, in_4);
  or or_1 (or_1_out, yimaqi3to8_1_out_5, yimaqi3to8_1_out_7, yimaqi3to8_1_out_8, yimaqi3to8_1_out_10, yimaqi3to8_1_out_11, yimaqi3to8_1_out_12, and_1_out, and_2_out);
  or or_2 (or_2_out, yimaqi3to8_1_out_5, yimaqi3to8_1_out_6, yimaqi3to8_1_out_7, yimaqi3to8_1_out_8, yimaqi3to8_1_out_9, yimaqi3to8_1_out_12, and_1_out, and_2_out);
  or or_3 (or_3_out, yimaqi3to8_1_out_5, yimaqi3to8_1_out_6, yimaqi3to8_1_out_8, yimaqi3to8_1_out_9, yimaqi3to8_1_out_10, yimaqi3to8_1_out_11, yimaqi3to8_1_out_12, and_1_out, and_2_out);
  or or_4 (or_4_out, yimaqi3to8_1_out_5, yimaqi3to8_1_out_7, yimaqi3to8_1_out_8, yimaqi3to8_1_out_10, yimaqi3to8_1_out_11, and_1_out, and_2_out);
  or or_5 (or_5_out, yimaqi3to8_1_out_5, yimaqi3to8_1_out_7, yimaqi3to8_1_out_11, and_1_out);
  or or_6 (or_6_out, yimaqi3to8_1_out_5, yimaqi3to8_1_out_9, yimaqi3to8_1_out_10, yimaqi3to8_1_out_11, and_1_out, and_2_out);
  or or_7 (or_7_out, yimaqi3to8_1_out_7, yimaqi3to8_1_out_8, yimaqi3to8_1_out_9, yimaqi3to8_1_out_10, yimaqi3to8_1_out_11, and_1_out, and_2_out);
  _7_Segment_Display u_7_segment_display_1 (
    .g(or_7_out), .f(or_6_out), .a(or_1_out), .b(or_2_out), .e(or_5_out), .d(or_4_out), .c(or_3_out));  // open: dp
endmodule

module shumaguanyimaqi16 (
  input  in_1,
  input  in_2,
  input  in_3,
  input  in_4
);

  wire not_1_out, or_1_out, or_2_out, or_3_out, or_4_out, or_5_out, or_6_out, or_7_out, or_8_out, or_9_out,
       or_10_out, or_11_out, or_12_out, or_13_out, or_14_out, yimaqi3to8_1_out_5, yimaqi3to8_1_out_6,
       yimaqi3to8_1_out_7, yimaqi3to8_1_out_8, yimaqi3to8_1_out_9, yimaqi3to8_1_out_10, yimaqi3to8_1_out_11,
       yimaqi3to8_1_out_12, yimaqi3to8_2_out_5, yimaqi3to8_2_out_6, yimaqi3to8_2_out_7, yimaqi3to8_2_out_8,
       yimaqi3to8_2_out_9, yimaqi3to8_2_out_10, yimaqi3to8_2_out_11, yimaqi3to8_2_out_12;

  not not_1 (not_1_out, in_4);
  yimaqi3to8 yimaqi3to8_1 (
    .zero(in_1), .one(in_2), .two(in_3), .en(not_1_out), .out_5(yimaqi3to8_1_out_5),
    .out_6(yimaqi3to8_1_out_6), .out_7(yimaqi3to8_1_out_7), .out_8(yimaqi3to8_1_out_8),
    .out_9(yimaqi3to8_1_out_9), .out_10(yimaqi3to8_1_out_10), .out_11(yimaqi3to8_1_out_11),
    .out_12(yimaqi3to8_1_out_12));
  yimaqi3to8 yimaqi3to8_2 (
    .zero(in_1), .one(in_2), .two(in_3), .en(in_4), .out_5(yimaqi3to8_2_out_5), .out_6(yimaqi3to8_2_out_6),
    .out_7(yimaqi3to8_2_out_7), .out_8(yimaqi3to8_2_out_8), .out_9(yimaqi3to8_2_out_9),
    .out_10(yimaqi3to8_2_out_10), .out_11(yimaqi3to8_2_out_11), .out_12(yimaqi3to8_2_out_12));
  or or_1 (or_1_out, yimaqi3to8_1_out_5, yimaqi3to8_1_out_7, yimaqi3to8_1_out_8, yimaqi3to8_1_out_10, yimaqi3to8_1_out_11, yimaqi3to8_1_out_12, yimaqi3to8_2_out_5, yimaqi3to8_2_out_6);
  or or_2 (or_2_out, yimaqi3to8_1_out_5, yimaqi3to8_1_out_6, yimaqi3to8_1_out_7, yimaqi3to8_1_out_8, yimaqi3to8_1_out_9, yimaqi3to8_1_out_12, yimaqi3to8_2_out_5, yimaqi3to8_2_out_6);
  or or_3 (or_3_out, yimaqi3to8_1_out_5, yimaqi3to8_1_out_6, yimaqi3to8_1_out_8, yimaqi3to8_1_out_9, yimaqi3to8_1_out_10, yimaqi3to8_1_out_11, yimaqi3to8_1_out_12, yimaqi3to8_2_out_5, yimaqi3to8_2_out_6);
  or or_4 (or_4_out, yimaqi3to8_1_out_5, yimaqi3to8_1_out_7, yimaqi3to8_1_out_8, yimaqi3to8_1_out_10, yimaqi3to8_1_out_11, yimaqi3to8_2_out_5, yimaqi3to8_2_out_6);
  or or_5 (or_5_out, yimaqi3to8_1_out_5, yimaqi3to8_1_out_7, yimaqi3to8_1_out_11, yimaqi3to8_2_out_5);
  or or_6 (or_6_out, yimaqi3to8_1_out_5, yimaqi3to8_1_out_9, yimaqi3to8_1_out_10, yimaqi3to8_1_out_11, yimaqi3to8_2_out_5, yimaqi3to8_2_out_6);
  or or_7 (or_7_out, yimaqi3to8_1_out_7, yimaqi3to8_1_out_8, yimaqi3to8_1_out_9, yimaqi3to8_1_out_10, yimaqi3to8_1_out_11, yimaqi3to8_2_out_5, yimaqi3to8_2_out_6);
  or or_8 (or_8_out, or_1_out, yimaqi3to8_2_out_7, yimaqi3to8_2_out_9, yimaqi3to8_2_out_11, yimaqi3to8_2_out_12);
  or or_9 (or_9_out, or_2_out, yimaqi3to8_2_out_7, yimaqi3to8_2_out_10);
  or or_10 (or_10_out, or_3_out, yimaqi3to8_2_out_7, yimaqi3to8_2_out_8, yimaqi3to8_2_out_10);
  or or_11 (or_11_out, or_4_out, yimaqi3to8_2_out_8, yimaqi3to8_2_out_9, yimaqi3to8_2_out_10, yimaqi3to8_2_out_11);
  _7_Segment_Display u_7_segment_display_1 (
    .g(or_14_out), .f(or_13_out), .a(or_8_out), .b(or_9_out), .e(or_12_out), .d(or_11_out), .c(or_10_out),
    .dp(or_10_out));
  or or_12 (or_12_out, or_5_out, yimaqi3to8_2_out_7, yimaqi3to8_2_out_8, yimaqi3to8_2_out_9, yimaqi3to8_2_out_10, yimaqi3to8_2_out_11, yimaqi3to8_2_out_12);
  or or_13 (or_13_out, or_6_out, yimaqi3to8_2_out_7, yimaqi3to8_2_out_8, yimaqi3to8_2_out_9, yimaqi3to8_2_out_11, yimaqi3to8_2_out_12);
  or or_14 (or_14_out, or_7_out, yimaqi3to8_2_out_7, yimaqi3to8_2_out_8, yimaqi3to8_2_out_10, yimaqi3to8_2_out_11, yimaqi3to8_2_out_12);
endmodule
